# Fritzing sketch Electrical (saved by Fritzing 0.9.3b)
circuit board: 8.46667cm x 5.64444cm
breadboards: 1

parts:
  Main_Board = Arduino Uno (Rev3)
  Left = Basic Servo
  Right = Basic Servo
  hc-sr1 = hc-sr04
  U1 = LIPO-1000mAh [package=lipo-1000]
  IC1 = Voltage Regulator [package=to220-igo]
  Flame = TSOP312.., 314.. [package=THT]

nets:
  GND: Main_Board.GND, hc-sr1.GND, U1.-, Flame.GND
  N1: Main_Board.D2, hc-sr1.Echo
  N2: Main_Board.D3_PWM, hc-sr1.Trig
  N3: Main_Board.D4, Left.pulse
  N4: Main_Board.D5_PWM, Right.pulse
  N5: Main_Board.D6_PWM, Flame.Data
  5V: Main_Board.5V, hc-sr1.VCC, U1.+, IC1.IN, Flame.Vs
  GND_2: Left.gnd, Right.gnd, IC1.GND
  VCC: Left.vcc, Right.vcc, IC1.OUT

custom parts:
  hc-sr04: This is a HC-SR04 Distance Sensor
